# Fritzing sketch Nightlight (saved by Fritzing 0.9.10b)
breadboards: 1

parts:
  R1 = PHOTOCELL [package=photocell-kit]
  R2 = Resistor [tolerance=±5% resistance=10k package="0805 [SMD]"]
  R4 = Resistor [tolerance=±5% resistance=220 package="0805 [SMD]"]
  Part1 = Arduino Uno (Rev3) - ICSP
  Grove1 = Grove OLED 128x96
  Mod1 = KY-015 Temperature & Humidity Sensor Module [package="Breakout board"]
  RGB_SMD_LED1 = SMD RGB LED (WS2812) [package=5050]
  RGB_SMD_LED2 = SMD RGB LED (WS2812) [package=5050]  # not connected
  RGB_SMD_LED3 = SMD RGB LED (WS2812) [package=5050]  # not connected
  PSU1 = Adjustable Breadboard Power Supply  # not connected
  FC-1 = Sound Sensor
  Part2 = Bluetooth HC-06 Macho
  R5 = Resistor [tolerance=±5% resistance=220 package="0805 [SMD]"]
  R6 = Resistor [tolerance=±5% resistance=220 package="0805 [SMD]"]

nets:
  N1: R1.P$1, R2.Pin_1, Part1.A0
  GND: R1.P$2, Part1.GND, FC-1.GND
  N2: R2.Pin_0, FC-1.VCC
  N3: R4.Pin_0, RGB_SMD_LED1.DIn
  N4: Part1.A2, FC-1.OUT
  N5: Part1.D10_PWM/SS, Mod1.S
  N6: Part1.A4/SDA, Grove1.SCL
  N7: Part1.A5/SCL, Grove1.SDA
  N8: Part1.D0/RX, Part2.TXD
  N9: Part1.D1/TX, R5.Pin_0
  GND_2: Grove1.GND, Mod1.Vin, RGB_SMD_LED1.DOut, Part2.GND, R6.Pin_0
  VCC: Grove1.VCC, Mod1.-, RGB_SMD_LED1.VCC, Part2.VCC
  N10: Part2.RXD, R5.Pin_1, R6.Pin_1

custom parts:
  KY-015 Temperature & Humidity Sensor Module: KY-015 temperature and humidity sensor module, provides a low-latency serial interface to measure humidity and temperature.
